# Fritzing sketch 4x4 Led Matrix with Arduino (saved by Fritzing 0.9.3b)
breadboards: 2

parts:
  LED1 = LED - 5mm [color="Red (633nm)" package="5 mm [THT]"]
  LED2 = LED - 5mm [color="Red (633nm)" package="5 mm [THT]"]
  LED3 = LED - 5mm [color="Red (633nm)" package="5 mm [THT]"]
  LED4 = LED - 5mm [color="Red (633nm)" package="5 mm [THT]"]
  LED5 = LED - 5mm [color="Red (633nm)" package="5 mm [THT]"]
  LED6 = LED - 5mm [color="Red (633nm)" package="5 mm [THT]"]
  LED7 = LED - 5mm [color="Red (633nm)" package="5 mm [THT]"]
  LED8 = LED - 5mm [color="Red (633nm)" package="5 mm [THT]"]
  LED9 = LED - 5mm [color="Red (633nm)" package="5 mm [THT]"]
  LED10 = LED - 5mm [color="Red (633nm)" package="5 mm [THT]"]
  LED11 = LED - 5mm [color="Red (633nm)" package="5 mm [THT]"]
  LED12 = LED - 5mm [color="Red (633nm)" package="5 mm [THT]"]
  LED13 = LED - 5mm [color="Red (633nm)" package="5 mm [THT]"]
  LED14 = LED - 5mm [color="Red (633nm)" package="5 mm [THT]"]
  LED15 = LED - 5mm [color="Red (633nm)" package="5 mm [THT]"]
  LED16 = LED - 5mm [color="Red (633nm)" package="5 mm [THT]"]
  U1 = 74HC595 [package="DIP16 [THT]"]  # not connected
  Part1 = Arduino Uno (Rev3)  # not connected

nets:
  N1: LED1.cathode, LED6.cathode, LED11.cathode, LED12.cathode
  N2: LED1.anode, LED2.anode, LED5.anode, LED15.anode
  N3: LED2.cathode, LED13.cathode, LED14.cathode, LED16.cathode
  N4: LED3.cathode, LED4.cathode, LED5.cathode, LED10.cathode
  N5: LED3.anode, LED7.anode, LED11.anode, LED14.anode
  N6: LED4.anode, LED8.anode, LED12.anode, LED13.anode
  N7: LED6.anode, LED9.anode, LED10.anode, LED16.anode
  N8: LED7.cathode, LED8.cathode, LED9.cathode, LED15.cathode
