# Fritzing sketch 4x4 RGB with 4x4 switches (saved by Fritzing 0.9.3b)
circuit board: 17.5976cm x 18.8033cm
breadboards: 1

parts:
  LED1 = RGB LED (com. cathode, rgb) [package="5 mm [THT]"]
  LED2 = RGB LED (com. cathode, rgb) [package="5 mm [THT]"]
  LED3 = RGB LED (com. cathode, rgb) [package="5 mm [THT]"]
  LED4 = RGB LED (com. cathode, rgb) [package="5 mm [THT]"]
  LED5 = RGB LED (com. cathode, rgb) [package="5 mm [THT]"]
  LED6 = RGB LED (com. cathode, rgb) [package="5 mm [THT]"]
  LED7 = RGB LED (com. cathode, rgb) [package="5 mm [THT]"]
  LED8 = RGB LED (com. cathode, rgb) [package="5 mm [THT]"]
  LED9 = RGB LED (com. cathode, rgb) [package="5 mm [THT]"]
  LED10 = RGB LED (com. cathode, rgb) [package="5 mm [THT]"]
  LED11 = RGB LED (com. cathode, rgb) [package="5 mm [THT]"]
  LED12 = RGB LED (com. cathode, rgb) [package="5 mm [THT]"]
  LED13 = RGB LED (com. cathode, rgb) [package="5 mm [THT]"]
  LED14 = RGB LED (com. cathode, rgb) [package="5 mm [THT]"]
  LED15 = RGB LED (com. cathode, rgb) [package="5 mm [THT]"]
  LED16 = RGB LED (com. cathode, rgb) [package="5 mm [THT]"]
  U1 = 74HC595 [package="DIP16 [THT]"]
  U2 = 74HC595 [package="DIP16 [THT]"]
  Part1 = Arduino Uno (Rev3)

nets:
  N1: LED1.red_anode, LED7.red_anode, LED14.red_anode, LED15.red_anode, U1.Q0
  N2: LED1.common_cathode, LED2.common_cathode, LED3.common_cathode, LED4.common_cathode
  N3: LED1.green_anode, LED7.green_anode, LED14.green_anode, LED15.green_anode, U1.Q4
  N4: LED1.blue_anode, LED7.blue_anode, LED14.blue_anode, LED15.blue_anode, U2.Q0
  N5: LED2.red_anode, LED8.red_anode, LED10.red_anode, LED16.red_anode, U1.Q1
  N6: LED2.green_anode, LED8.green_anode, LED10.green_anode, LED16.green_anode, U1.Q5
  N7: LED2.blue_anode, LED8.blue_anode, LED10.blue_anode, LED16.blue_anode, U2.Q1
  N8: LED3.red_anode, LED6.red_anode, LED9.red_anode, LED13.red_anode, U1.Q2
  N9: LED3.green_anode, LED6.green_anode, LED9.green_anode, LED13.green_anode, U1.Q6
  N10: LED3.blue_anode, LED6.blue_anode, LED9.blue_anode, LED13.blue_anode, U2.Q2
  N11: LED4.red_anode, LED5.red_anode, LED11.red_anode, LED12.red_anode, U1.Q3
  N12: LED4.green_anode, LED5.green_anode, LED11.green_anode, LED12.green_anode, U1.Q7
  N13: LED4.blue_anode, LED5.blue_anode, LED11.blue_anode, LED12.blue_anode, U2.Q3, U2.Q7
  N14: LED5.common_cathode, LED6.common_cathode, LED7.common_cathode, LED8.common_cathode, U2.Q6
  N15: LED9.common_cathode, LED10.common_cathode, LED11.common_cathode, LED14.common_cathode, U2.Q5
  N16: LED12.common_cathode, LED13.common_cathode, LED15.common_cathode, LED16.common_cathode, U2.Q4
  GND: U1.GND, U2.GND, Part1.GND
  VCC: U1.MR, U1.VCC, U2.MR, U2.VCC, Part1.5V
  N17: U1.DS, U2.Q7'
