# Fritzing sketch 4x4 switch breakout Board (saved by Fritzing 0.9.3b)
circuit board: 7.2509cm x 9.98439cm
breadboards: 1

parts:
  S1 = Pushbutton [package="[THT]"]
  S2 = Pushbutton [package="[THT]"]
  S3 = Pushbutton [package="[THT]"]
  S4 = Pushbutton [package="[THT]"]
  S5 = Pushbutton [package="[THT]"]
  S6 = Pushbutton [package="[THT]"]
  S7 = Pushbutton [package="[THT]"]
  S8 = Pushbutton [package="[THT]"]
  S9 = Pushbutton [package="[THT]"]
  S10 = Pushbutton [package="[THT]"]
  S11 = Pushbutton [package="[THT]"]
  S12 = Pushbutton [package="[THT]"]
  S13 = Pushbutton [package="[THT]"]
  S14 = Pushbutton [package="[THT]"]
  S15 = Pushbutton [package="[THT]"]
  S16 = Pushbutton [package="[THT]"]
  IC1 = IC, DIP package, 16 pins [chip_label=IC]
  VCC1 = Battery

nets:
  N1: S1.Pin_1, S1.Pin_2, S2.Pin_1, S2.Pin_2, S3.Pin_1, S3.Pin_2, S4.Pin_1, S4.Pin_2, S5.Pin_1, S5.Pin_2, S6.Pin_1, S6.Pin_2, S7.Pin_1, S7.Pin_2, S8.Pin_1, S8.Pin_2, S9.Pin_1, S9.Pin_2, S10.Pin_1, S10.Pin_2, S11.Pin_1, S11.Pin_2, S12.Pin_1, S12.Pin_2, S13.Pin_1, S13.Pin_2, S14.Pin_1, S14.Pin_2, S15.Pin_1, S15.Pin_2, S16.Pin_1, S16.Pin_2, IC1.pin1, IC1.pin2, IC1.pin3, IC1.pin4, IC1.pin5, IC1.pin6, IC1.pin7, IC1.pin8
  N2: S1.Pin_3, S1.Pin_4, S2.Pin_4, S3.Pin_4, S4.Pin_3, S4.Pin_4, S5.Pin_4, S6.Pin_4, S7.Pin_4, S8.Pin_3, S8.Pin_4, S9.Pin_4, S10.Pin_4, S11.Pin_4, S12.Pin_4, S13.Pin_4, S14.Pin_4, S15.Pin_4, S16.Pin_4, IC1.pin16, VCC1.+
  N3: IC1.pin14, IC1.pin15, VCC1.-
