# Fritzing sketch LED multiplexing (saved by Fritzing 0.9.3b)
breadboards: 3

parts:
  Part1 = Arduino Uno (Rev3)  # not connected
  LED14 = RGB LED (com. cathode, rgb) [package="5 mm [THT]"]
  LED15 = RGB LED (com. cathode, rgb) [package="5 mm [THT]"]
  LED18 = RGB LED (com. cathode, rgb) [package="5 mm [THT]"]
  LED20 = RGB LED (com. cathode, rgb) [package="5 mm [THT]"]
  LED21 = RGB LED (com. cathode, rgb) [package="5 mm [THT]"]
  LED22 = RGB LED (com. cathode, rgb) [package="5 mm [THT]"]
  LED24 = RGB LED (com. cathode, rgb) [package="5 mm [THT]"]
  LED26 = RGB LED (com. cathode, rgb) [package="5 mm [THT]"]
  U1 = 74HC595 [package="DIP16 [THT]"]
  U2 = 74HC595 [package="DIP16 [THT]"]
  U3 = 74HC595 [package="DIP16 [THT]"]
  U4 = 74HC595 [package="DIP16 [THT]"]
  LED36 = RGB LED (com. cathode, rgb) [package="5 mm [THT]"]
  LED38 = RGB LED (com. cathode, rgb) [package="5 mm [THT]"]
  LED40 = RGB LED (com. cathode, rgb) [package="5 mm [THT]"]
  LED41 = RGB LED (com. cathode, rgb) [package="5 mm [THT]"]
  LED42 = RGB LED (com. cathode, rgb) [package="5 mm [THT]"]
  LED43 = RGB LED (com. cathode, rgb) [package="5 mm [THT]"]
  LED39 = RGB LED (com. cathode, rgb) [package="5 mm [THT]"]
  LED44 = RGB LED (com. cathode, rgb) [package="5 mm [THT]"]
  LED45 = RGB LED (com. cathode, rgb) [package="5 mm [THT]"]
  LED32 = RGB LED (com. cathode, rgb) [package="5 mm [THT]"]
  LED31 = RGB LED (com. cathode, rgb) [package="5 mm [THT]"]
  LED34 = RGB LED (com. cathode, rgb) [package="5 mm [THT]"]
  LED37 = RGB LED (com. cathode, rgb) [package="5 mm [THT]"]
  LED33 = RGB LED (com. cathode, rgb) [package="5 mm [THT]"]
  LED30 = RGB LED (com. cathode, rgb) [package="5 mm [THT]"]
  LED35 = RGB LED (com. cathode, rgb) [package="5 mm [THT]"]
  LED19 = RGB LED (com. cathode, rgb) [package="5 mm [THT]"]
  LED25 = RGB LED (com. cathode, rgb) [package="5 mm [THT]"]
  LED28 = RGB LED (com. cathode, rgb) [package="5 mm [THT]"]
  LED16 = RGB LED (com. cathode, rgb) [package="5 mm [THT]"]
  LED23 = RGB LED (com. cathode, rgb) [package="5 mm [THT]"]
  LED29 = RGB LED (com. cathode, rgb) [package="5 mm [THT]"]
  LED27 = RGB LED (com. cathode, rgb) [package="5 mm [THT]"]
  LED17 = RGB LED (com. cathode, rgb) [package="5 mm [THT]"]
  R17 = Resistor [tolerance=±5% resistance=220 package=THT]
  R18 = Resistor [tolerance=±5% resistance=220 package=THT]
  R19 = Resistor [tolerance=±5% resistance=220 package=THT]

nets:
  N1: LED14.red_anode, LED33.red_anode, LED30.red_anode, LED17.red_anode
  N2: LED14.common_cathode, U1.Q7
  N3: LED14.green_anode, LED33.green_anode, LED30.green_anode, LED17.green_anode
  N4: LED14.blue_anode, LED33.blue_anode, LED30.blue_anode, LED17.blue_anode
  N5: LED15.red_anode, LED31.red_anode, LED35.red_anode, LED19.red_anode
  N6: LED15.common_cathode, U1.Q5
  N7: LED15.green_anode, LED31.green_anode, LED35.green_anode, LED19.green_anode
  N8: LED15.blue_anode, LED31.blue_anode, LED35.blue_anode, LED19.blue_anode
  N9: LED18.red_anode, LED44.red_anode, LED34.red_anode, LED25.red_anode
  N10: LED18.common_cathode, U1.Q6
  N11: LED18.green_anode, LED44.green_anode, LED34.green_anode, LED25.green_anode
  N12: LED18.blue_anode, LED44.blue_anode, LED34.blue_anode, LED25.blue_anode
  N13: LED20.red_anode, LED43.red_anode, LED39.red_anode, LED23.red_anode
  N14: LED20.common_cathode, U1.Q3
  N15: LED20.green_anode, LED43.green_anode, LED39.green_anode, LED23.green_anode
  N16: LED20.blue_anode, LED43.blue_anode, LED39.blue_anode, LED23.blue_anode
  N17: LED21.red_anode, LED38.red_anode, LED41.red_anode, LED27.red_anode
  N18: LED21.common_cathode, U1.Q2
  N19: LED21.green_anode, LED38.green_anode, LED41.green_anode, LED27.green_anode
  N20: LED21.blue_anode, LED38.blue_anode, LED41.blue_anode, LED27.blue_anode
  N21: LED22.red_anode, LED40.red_anode, LED42.red_anode, LED28.red_anode
  N22: LED22.common_cathode, U1.Q1
  N23: LED22.green_anode, LED40.green_anode, LED42.green_anode, LED28.green_anode
  N24: LED22.blue_anode, LED40.blue_anode, LED42.blue_anode, LED28.blue_anode
  N25: LED24.red_anode, LED36.red_anode, LED37.red_anode, LED29.red_anode, R17.Pin_0
  N26: LED24.common_cathode, U1.Q0
  N27: LED24.green_anode, LED36.green_anode, LED37.green_anode, LED29.green_anode, R18.Pin_0
  N28: LED24.blue_anode, LED36.blue_anode, LED37.blue_anode, LED29.blue_anode, R19.Pin_0
  N29: LED26.red_anode, LED45.red_anode, LED32.red_anode, LED16.red_anode
  N30: LED26.common_cathode, U1.Q4
  N31: LED26.green_anode, LED45.green_anode, LED32.green_anode, LED16.green_anode
  N32: LED26.blue_anode, LED45.blue_anode, LED32.blue_anode, LED16.blue_anode
  GND: U1.GND, U2.GND, U3.GND, U4.GND
  VCC: U1.VCC, U2.VCC, U3.VCC, U4.VCC
  N33: U2.Q1, LED28.common_cathode
  N34: U2.Q2, LED27.common_cathode
  N35: U2.Q3, LED23.common_cathode
  N36: U2.Q4, LED16.common_cathode
  N37: U2.Q5, LED19.common_cathode
  N38: U2.Q6, LED25.common_cathode
  N39: U2.Q7, LED17.common_cathode
  N40: U2.Q0, LED29.common_cathode
  N41: U3.Q1, LED40.common_cathode
  N42: U3.Q2, LED38.common_cathode
  N43: U3.Q3, LED39.common_cathode
  N44: U3.Q4, LED32.common_cathode
  N45: U3.Q5, LED35.common_cathode
  N46: U3.Q6, LED44.common_cathode
  N47: U3.Q7, LED33.common_cathode
  N48: U3.Q0, LED36.common_cathode
  N49: U4.Q1, LED42.common_cathode
  N50: U4.Q2, LED41.common_cathode
  N51: U4.Q3, LED43.common_cathode
  N52: U4.Q4, LED45.common_cathode
  N53: U4.Q5, LED31.common_cathode
  N54: U4.Q6, LED34.common_cathode
  N55: U4.Q7, LED30.common_cathode
  N56: U4.Q0, LED37.common_cathode
