# Fritzing sketch Rigger Launchpad PCB (saved by Fritzing 0.9.3b)
circuit board: 21.9569cm x 26.5822cm
breadboards: 1

parts:
  LED61 = LED - 5mm [color="Red (633nm)" package="5 mm [THT]"]
  S40 = Pushbutton [package="[THT]"]
  LED62 = LED - 5mm [color="Red (633nm)" package="5 mm [THT]"]
  S41 = Pushbutton [package="[THT]"]
  LED63 = LED - 5mm [color="Red (633nm)" package="5 mm [THT]"]
  LED64 = LED - 5mm [color="Red (633nm)" package="5 mm [THT]"]
  S42 = Pushbutton [package="[THT]"]
  S43 = Pushbutton [package="[THT]"]
  LED65 = LED - 5mm [color="Red (633nm)" package="5 mm [THT]"]
  LED66 = LED - 5mm [color="Red (633nm)" package="5 mm [THT]"]
  LED67 = LED - 5mm [color="Red (633nm)" package="5 mm [THT]"]
  LED68 = LED - 5mm [color="Red (633nm)" package="5 mm [THT]"]
  S44 = Pushbutton [package="[THT]"]
  S45 = Pushbutton [package="[THT]"]
  S46 = Pushbutton [package="[THT]"]
  S47 = Pushbutton [package="[THT]"]
  LED69 = LED - 5mm [color="Red (633nm)" package="5 mm [THT]"]
  LED70 = LED - 5mm [color="Red (633nm)" package="5 mm [THT]"]
  LED71 = LED - 5mm [color="Red (633nm)" package="5 mm [THT]"]
  LED72 = LED - 5mm [color="Red (633nm)" package="5 mm [THT]"]
  LED73 = LED - 5mm [color="Red (633nm)" package="5 mm [THT]"]
  LED74 = LED - 5mm [color="Red (633nm)" package="5 mm [THT]"]
  LED75 = LED - 5mm [color="Red (633nm)" package="5 mm [THT]"]
  LED76 = LED - 5mm [color="Red (633nm)" package="5 mm [THT]"]
  S48 = Pushbutton [package="[THT]"]
  S49 = Pushbutton [package="[THT]"]
  S50 = Pushbutton [package="[THT]"]
  S51 = Pushbutton [package="[THT]"]
  S52 = Pushbutton [package="[THT]"]
  S53 = Pushbutton [package="[THT]"]
  S54 = Pushbutton [package="[THT]"]
  S55 = Pushbutton [package="[THT]"]
  LED77 = LED - 5mm [color="Red (633nm)" package="5 mm [THT]"]
  LED78 = LED - 5mm [color="Red (633nm)" package="5 mm [THT]"]
  LED79 = LED - 5mm [color="Red (633nm)" package="5 mm [THT]"]
  LED80 = LED - 5mm [color="Red (633nm)" package="5 mm [THT]"]
  LED81 = LED - 5mm [color="Red (633nm)" package="5 mm [THT]"]
  LED82 = LED - 5mm [color="Red (633nm)" package="5 mm [THT]"]
  LED83 = LED - 5mm [color="Red (633nm)" package="5 mm [THT]"]
  LED84 = LED - 5mm [color="Red (633nm)" package="5 mm [THT]"]
  LED85 = LED - 5mm [color="Red (633nm)" package="5 mm [THT]"]
  LED86 = LED - 5mm [color="Red (633nm)" package="5 mm [THT]"]
  LED87 = LED - 5mm [color="Red (633nm)" package="5 mm [THT]"]
  LED88 = LED - 5mm [color="Red (633nm)" package="5 mm [THT]"]
  LED89 = LED - 5mm [color="Red (633nm)" package="5 mm [THT]"]
  LED90 = LED - 5mm [color="Red (633nm)" package="5 mm [THT]"]
  LED91 = LED - 5mm [color="Red (633nm)" package="5 mm [THT]"]
  LED92 = LED - 5mm [color="Red (633nm)" package="5 mm [THT]"]
  S56 = Pushbutton [package="[THT]"]
  S57 = Pushbutton [package="[THT]"]
  S58 = Pushbutton [package="[THT]"]
  S59 = Pushbutton [package="[THT]"]
  S60 = Pushbutton [package="[THT]"]
  S61 = Pushbutton [package="[THT]"]
  S62 = Pushbutton [package="[THT]"]
  S63 = Pushbutton [package="[THT]"]
  S64 = Pushbutton [package="[THT]"]
  S65 = Pushbutton [package="[THT]"]
  S66 = Pushbutton [package="[THT]"]
  S67 = Pushbutton [package="[THT]"]
  S68 = Pushbutton [package="[THT]"]
  S69 = Pushbutton [package="[THT]"]
  S70 = Pushbutton [package="[THT]"]
  S71 = Pushbutton [package="[THT]"]
  LED93 = LED - 5mm [color="Red (633nm)" package="5 mm [THT]"]
  LED94 = LED - 5mm [color="Red (633nm)" package="5 mm [THT]"]
  LED95 = LED - 5mm [color="Red (633nm)" package="5 mm [THT]"]
  LED96 = LED - 5mm [color="Red (633nm)" package="5 mm [THT]"]
  LED97 = LED - 5mm [color="Red (633nm)" package="5 mm [THT]"]
  LED98 = LED - 5mm [color="Red (633nm)" package="5 mm [THT]"]
  LED99 = LED - 5mm [color="Red (633nm)" package="5 mm [THT]"]
  LED100 = LED - 5mm [color="Red (633nm)" package="5 mm [THT]"]
  LED101 = LED - 5mm [color="Red (633nm)" package="5 mm [THT]"]
  LED102 = LED - 5mm [color="Red (633nm)" package="5 mm [THT]"]
  LED103 = LED - 5mm [color="Red (633nm)" package="5 mm [THT]"]
  LED104 = LED - 5mm [color="Red (633nm)" package="5 mm [THT]"]
  LED105 = LED - 5mm [color="Red (633nm)" package="5 mm [THT]"]
  LED106 = LED - 5mm [color="Red (633nm)" package="5 mm [THT]"]
  LED107 = LED - 5mm [color="Red (633nm)" package="5 mm [THT]"]
  LED108 = LED - 5mm [color="Red (633nm)" package="5 mm [THT]"]
  LED109 = LED - 5mm [color="Red (633nm)" package="5 mm [THT]"]
  LED110 = LED - 5mm [color="Red (633nm)" package="5 mm [THT]"]
  LED111 = LED - 5mm [color="Red (633nm)" package="5 mm [THT]"]
  LED112 = LED - 5mm [color="Red (633nm)" package="5 mm [THT]"]
  LED113 = LED - 5mm [color="Red (633nm)" package="5 mm [THT]"]
  LED114 = LED - 5mm [color="Red (633nm)" package="5 mm [THT]"]
  LED115 = LED - 5mm [color="Red (633nm)" package="5 mm [THT]"]
  LED116 = LED - 5mm [color="Red (633nm)" package="5 mm [THT]"]
  LED117 = LED - 5mm [color="Red (633nm)" package="5 mm [THT]"]
  LED118 = LED - 5mm [color="Red (633nm)" package="5 mm [THT]"]
  LED119 = LED - 5mm [color="Red (633nm)" package="5 mm [THT]"]
  LED120 = LED - 5mm [color="Red (633nm)" package="5 mm [THT]"]
  LED121 = LED - 5mm [color="Red (633nm)" package="5 mm [THT]"]
  LED122 = LED - 5mm [color="Red (633nm)" package="5 mm [THT]"]
  LED123 = LED - 5mm [color="Red (633nm)" package="5 mm [THT]"]
  LED124 = LED - 5mm [color="Red (633nm)" package="5 mm [THT]"]
  S72 = Pushbutton [package="[THT]"]
  S73 = Pushbutton [package="[THT]"]
  S74 = Pushbutton [package="[THT]"]
  S75 = Pushbutton [package="[THT]"]
  S76 = Pushbutton [package="[THT]"]
  S77 = Pushbutton [package="[THT]"]
  S78 = Pushbutton [package="[THT]"]
  S79 = Pushbutton [package="[THT]"]
  S80 = Pushbutton [package="[THT]"]
  S81 = Pushbutton [package="[THT]"]
  S82 = Pushbutton [package="[THT]"]
  S83 = Pushbutton [package="[THT]"]
  S84 = Pushbutton [package="[THT]"]
  S85 = Pushbutton [package="[THT]"]
  S86 = Pushbutton [package="[THT]"]
  S87 = Pushbutton [package="[THT]"]
  S88 = Pushbutton [package="[THT]"]
  S89 = Pushbutton [package="[THT]"]
  S90 = Pushbutton [package="[THT]"]
  S91 = Pushbutton [package="[THT]"]
  S92 = Pushbutton [package="[THT]"]
  S93 = Pushbutton [package="[THT]"]
  S94 = Pushbutton [package="[THT]"]
  S95 = Pushbutton [package="[THT]"]
  S96 = Pushbutton [package="[THT]"]
  S97 = Pushbutton [package="[THT]"]
  S98 = Pushbutton [package="[THT]"]
  S99 = Pushbutton [package="[THT]"]
  S100 = Pushbutton [package="[THT]"]
  S101 = Pushbutton [package="[THT]"]
  S102 = Pushbutton [package="[THT]"]
  S103 = Pushbutton [package="[THT]"]

nets:
  N1: LED61.cathode, LED62.cathode, LED63.cathode, LED65.cathode, LED66.cathode, LED67.cathode, LED68.cathode
  N2: LED61.anode, LED76.anode, LED79.anode, LED81.anode, LED101.anode, LED102.anode, LED122.anode, LED123.anode
  N3: S40.Pin_1, S40.Pin_2, S41.Pin_1, S41.Pin_2, S42.Pin_1, S42.Pin_2, S43.Pin_1, S43.Pin_2, S44.Pin_1, S44.Pin_2, S45.Pin_1, S45.Pin_2, S46.Pin_1, S46.Pin_2, S47.Pin_1, S47.Pin_2
  N4: LED62.anode, LED74.anode, LED83.anode, LED89.anode, LED103.anode, LED106.anode, LED114.anode, LED115.anode
  N5: LED63.anode, LED70.anode, LED80.anode, LED88.anode, LED107.anode, LED108.anode, LED120.anode, LED121.anode
  N6: LED64.anode, LED73.anode, LED82.anode, LED91.anode, LED98.anode, LED109.anode, LED112.anode, LED124.anode
  N7: LED65.anode, LED77.anode, LED84.anode, LED93.anode, LED110.anode, LED118.anode, LED119.anode
  N8: LED66.anode, LED72.anode, LED85.anode, LED92.anode, LED111.anode, LED113.anode, LED116.anode, LED117.anode
  N9: LED67.anode, LED71.anode, LED78.anode, LED87.anode, LED94.anode, LED99.anode, LED104.anode, LED105.anode
  N10: LED68.anode, LED69.anode, LED86.anode, LED90.anode, LED95.anode, LED96.anode, LED97.anode, LED100.anode
  N11: LED69.cathode, LED70.cathode, LED71.cathode, LED72.cathode, LED73.cathode, LED74.cathode, LED75.cathode, LED76.cathode
  N12: S48.Pin_1, S48.Pin_2, S49.Pin_1, S49.Pin_2, S50.Pin_1, S50.Pin_2, S51.Pin_1, S51.Pin_2, S52.Pin_1, S52.Pin_2, S53.Pin_1, S53.Pin_2, S54.Pin_1, S54.Pin_2, S55.Pin_1, S55.Pin_2
  N13: LED77.cathode, LED78.cathode, LED81.cathode, LED82.cathode, LED83.cathode, LED85.cathode, LED86.cathode, LED88.cathode
  N14: LED79.cathode, LED80.cathode, LED84.cathode, LED87.cathode, LED89.cathode, LED90.cathode, LED91.cathode, LED92.cathode
  N15: S56.Pin_1, S56.Pin_2, S59.Pin_1, S59.Pin_2, S60.Pin_1, S60.Pin_2, S61.Pin_1, S61.Pin_2, S62.Pin_1, S62.Pin_2, S64.Pin_1, S64.Pin_2, S65.Pin_1, S65.Pin_2, S66.Pin_1, S66.Pin_2
  N16: S57.Pin_1, S57.Pin_2, S58.Pin_1, S58.Pin_2, S63.Pin_1, S63.Pin_2, S67.Pin_1, S67.Pin_2, S68.Pin_1, S68.Pin_2, S69.Pin_1, S69.Pin_2, S70.Pin_1, S70.Pin_2, S71.Pin_1, S71.Pin_2
  N17: LED93.cathode, LED95.cathode, LED101.cathode, LED105.cathode, LED106.cathode, LED108.cathode, LED109.cathode, LED117.cathode
  N18: LED94.cathode, LED96.cathode, LED98.cathode, LED102.cathode, LED107.cathode, LED110.cathode, LED114.cathode, LED116.cathode
  N19: LED97.cathode, LED112.cathode, LED113.cathode, LED115.cathode, LED119.cathode, LED121.cathode, LED123.cathode
  N20: LED100.cathode, LED103.cathode, LED104.cathode, LED111.cathode, LED118.cathode, LED120.cathode, LED122.cathode, LED124.cathode
  N21: S72.Pin_1, S72.Pin_2, S74.Pin_1, S74.Pin_2, S80.Pin_1, S80.Pin_2, S87.Pin_1, S87.Pin_2, S88.Pin_1, S88.Pin_2, S89.Pin_1, S89.Pin_2, S98.Pin_1, S98.Pin_2, S101.Pin_1, S101.Pin_2
  N22: S73.Pin_1, S73.Pin_2, S79.Pin_1, S79.Pin_2, S82.Pin_1, S82.Pin_2, S85.Pin_1, S85.Pin_2, S91.Pin_1, S91.Pin_2, S95.Pin_1, S95.Pin_2, S96.Pin_1, S96.Pin_2, S103.Pin_1, S103.Pin_2
  N23: S75.Pin_1, S75.Pin_2, S76.Pin_1, S76.Pin_2, S78.Pin_1, S78.Pin_2, S81.Pin_1, S81.Pin_2, S86.Pin_1, S86.Pin_2, S92.Pin_1, S92.Pin_2, S97.Pin_1, S97.Pin_2, S99.Pin_1, S99.Pin_2
  N24: S77.Pin_1, S77.Pin_2, S83.Pin_1, S83.Pin_2, S84.Pin_1, S84.Pin_2, S90.Pin_1, S90.Pin_2, S93.Pin_1, S93.Pin_2, S94.Pin_1, S94.Pin_2, S100.Pin_1, S100.Pin_2, S102.Pin_1, S102.Pin_2
