# Fritzing sketch Untitled Sketch 4 (saved by Fritzing 0.9.3b)
circuit board: 8.61801cm x 11.9017cm
breadboards: 1

parts:
  LED1 = RGB LED (com. cathode, rgb) [package="5 mm [THT]"]
  LED2 = RGB LED (com. cathode, rgb) [package="5 mm [THT]"]
  LED3 = RGB LED (com. cathode, rgb) [package="5 mm [THT]"]
  LED4 = RGB LED (com. cathode, rgb) [package="5 mm [THT]"]
  LED5 = RGB LED (com. cathode, rgb) [package="5 mm [THT]"]
  LED6 = RGB LED (com. cathode, rgb) [package="5 mm [THT]"]
  LED7 = RGB LED (com. cathode, rgb) [package="5 mm [THT]"]
  LED8 = RGB LED (com. cathode, rgb) [package="5 mm [THT]"]
  LED9 = RGB LED (com. cathode, rgb) [package="5 mm [THT]"]
  LED10 = RGB LED (com. cathode, rgb) [package="5 mm [THT]"]
  LED11 = RGB LED (com. cathode, rgb) [package="5 mm [THT]"]
  LED12 = RGB LED (com. cathode, rgb) [package="5 mm [THT]"]
  LED13 = RGB LED (com. cathode, rgb) [package="5 mm [THT]"]
  LED14 = RGB LED (com. cathode, rgb) [package="5 mm [THT]"]
  LED15 = RGB LED (com. cathode, rgb) [package="5 mm [THT]"]
  LED16 = RGB LED (com. cathode, rgb) [package="5 mm [THT]"]
  U1 = 74HC595 [package="DIP16 [THT]"]
  U2 = 74HC595 [package="DIP16 [THT]"]  # not connected

nets:
  N1: LED1.red_anode, LED5.red_anode, LED9.red_anode, LED13.red_anode, U1.Q0
  N2: LED1.common_cathode, LED2.common_cathode, LED3.common_cathode, LED4.common_cathode
  N3: LED1.green_anode, LED5.green_anode, LED9.green_anode, LED13.green_anode
  N4: LED1.blue_anode, LED5.blue_anode, LED9.blue_anode, LED13.blue_anode
  N5: LED2.red_anode, LED5.common_cathode, LED6.red_anode, LED10.red_anode, LED14.red_anode
  N6: LED2.green_anode, LED6.green_anode, LED10.green_anode, LED14.green_anode
  N7: LED2.blue_anode, LED6.blue_anode, LED10.blue_anode, LED14.blue_anode
  N8: LED3.red_anode, LED7.red_anode, LED11.red_anode, LED15.red_anode
  N9: LED3.green_anode, LED7.green_anode, LED11.green_anode, LED15.green_anode
  N10: LED3.blue_anode, LED7.blue_anode, LED11.blue_anode, LED15.blue_anode
  N11: LED4.red_anode, LED6.common_cathode, LED7.common_cathode, LED8.red_anode, LED12.red_anode, LED16.red_anode
  N12: LED4.green_anode, LED8.green_anode, LED12.green_anode, LED16.green_anode
  N13: LED4.blue_anode, LED8.blue_anode, LED12.blue_anode, LED16.blue_anode
  N14: LED9.common_cathode, LED10.common_cathode, LED11.common_cathode, LED12.common_cathode
  N15: LED13.common_cathode, LED15.common_cathode, LED16.common_cathode
